# Fritzing sketch csipesz_jelzo_receiver (saved by Fritzing 0.9.3b)
circuit board: 4.5cm x 1.8cm
breadboards: 1

parts:
  U1 = ATTINY45 [package=dip]
  J2 = female pin header, 3 pins [form="♀ (female)"]
  J1 = female pin header, 2 pins [form="♀ (female)"]
  J3 = female pin header, 3 pins [form="♀ (female)"]

nets:
  N1: U1.PB3(ADC3), J2.pin1
  N2: U1.GND, J2.pin2, J1.pin2, J3.pin3
  N3: U1.PB2(SCK_ADC1), J3.pin1
  N4: U1.VCC, J2.pin3, J1.pin1, J3.pin2

notes:
  -
  +
